# Fritzing sketch RIS fritz (saved by Fritzing 0.9.5d)
circuit board: 8.46667cm x 5.64444cm
breadboards: 1

parts:
  M1 = DOIT Esp32 DevKit v1 (30 pins long, 11 pins width) [part_number=ESP32S-PIN30]
  microSD1 = MicroSD Card Module
  ZS-042_RTC1 = ZS-042 RTC Module
  A1 = CJMCU-1220 module

nets:
  VCC: M1.3V3, microSD1.VCC, ZS-042_RTC1.VCC, A1.Pin_7, A1.Pin_10, A1.Pin_11
  N1: M1.D5, A1.Pin_5
  N2: M1.D18, microSD1.SCK, A1.Pin_4
  N3: M1.D19, microSD1.MISO, A1.Pin_2
  N4: M1.D21, ZS-042_RTC1.SDA
  N5: M1.D22, ZS-042_RTC1.SCL
  N6: M1.D23, microSD1.MOSI, A1.Pin_3
  N7: M1.D32, microSD1.CS
  GND: M1.GND, microSD1.GND, ZS-042_RTC1.GND, A1.Pin_8, A1.Pin_9, A1.Pin_12

notes:
  Pino do DS3231
  Pino do ESP32
  VCC
  3V3
  GND
  GND
  SDA
  GPIO 21
  SCL
  GPIO 22
  Pino do MicroSD
  Pino do ESP32
  VCC
  3V3
  GND
  GND
  MISO
  GPIO 19
  MOSI
  GPIO 23
  CS GPIO 32
  SCK GPIO 18
  Pino do ADS1220
  Pino do ESP32
  DVDD
  3V3
  AVDD
  3V3
  DGND
  GND
  AGND
  GND
  SCLK GPIO18
  MOSI GPIO 23
  MISO GPIO 19
  CS GPIO 5
  DRDY GPIO 4
  CLK N/A
  REFP0 3V3
  REFN0 GND
  AIN0 SINAL
  AIN1 SINAL

custom parts:
  DOIT Esp32 DevKit v1 (30 pins long, 11 pins width): The DOIT Esp32 DevKit v1 is one of the development board created by DOIT to evaluate the ESP-WROOM-32 module. It is based on the ESP32 microcontroller that boasts Wifi, Bluetooth, Ethernet and Low Power support all in a single chip. (vanepp) made breadboard work, adjusted pin numbering and labels and reduced size of schematic and cleaned up pcb. This chip is 30pins long (2 x15) and 11 pins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
  CJMCU-1220 module: The ADS1220 is a precision 24-bit analog-to-digital converter (ADC) that provides many integrated features to reduce system cost and component count for small sensor signals.
