# Fritzing sketch Teste ADS1220 (saved by Fritzing 0.9.5d)
breadboards: 1

parts:
  M1 = DOIT Esp32 DevKit v1 (30 pins long, 11 pins width) [part_number=ESP32S-PIN30]
  A1 = CJMCU-1220 module

nets:
  N1: M1.3V3, A1.Pin_7, A1.Pin_10, A1.Pin_11
  N2: M1.GND, A1.Pin_8, A1.Pin_12
  N3: M1.D4, A1.Pin_1
  N4: M1.D5, A1.Pin_5
  N5: M1.D18, A1.Pin_4
  N6: M1.D19, A1.Pin_2
  N7: M1.D23, A1.Pin_3

notes:
  Pino do ADS1220
  Pino do ESP32
  DVDD
  3V3
  AVDD
  3V3
  DGND
  GND
  AGND
  GND
  SCLK GPIO18
  MOSI GPIO 23
  MISO GPIO 19
  CS GPIO 5
  DRDY GPIO 4
  CLK N/A
  REFP0 3V3
  REFN0 GND
  AIN0 SINAL
  AIN1 SINAL

custom parts:
  DOIT Esp32 DevKit v1 (30 pins long, 11 pins width): The DOIT Esp32 DevKit v1 is one of the development board created by DOIT to evaluate the ESP-WROOM-32 module. It is based on the ESP32 microcontroller that boasts Wifi, Bluetooth, Ethernet and Low Power support all in a single chip. (vanepp) made breadboard work, adjusted pin numbering and labels and reduced size of schematic and cleaned up pcb. This chip is 30pins long (2 x15) and 11 pins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
  CJMCU-1220 module: The ADS1220 is a precision 24-bit analog-to-digital converter (ADC) that provides many integrated features to reduce system cost and component count for small sensor signals.
